# Fritzing sketch pushbutton-rp2040 (saved by Fritzing 1.0.2b)
breadboards: 1

parts:
  A1 = Waveshare rp2040-zero tht [package=THT]
  S2 = Pushbutton [package="[THT]"]
  S1 = Pushbutton [package="[THT]"]

nets:
  N1: A1.Pin_2, S2.Pin_1, S2.Pin_2, S1.Pin_1, S1.Pin_2
  N2: A1.Pin_16, S1.Pin_3, S1.Pin_4
  N3: A1.Pin_17, S2.Pin_3, S2.Pin_4

custom parts:
  Waveshare rp2040-zero tht: .RP2040-Zero, A Low-Cost, High-Performance Pico-Like MCU Board Based On Raspberry Pi Microcontroller RP2040. This varant is THT without the extra connections.
